# Fritzing sketch FCU_EFIS (saved by Fritzing 0.9.5d)

parts:
  Bauteil1 = Adafruit TCA9548A
  OLED1 = OLED 128x64 I2C Monochrome Display
  OLED2 = OLED 128x64 I2C Monochrome Display
  OLED3 = OLED 128x64 I2C Monochrome Display
  OLED4 = OLED 128x64 I2C Monochrome Display
  OLED5 = OLED 128x64 I2C Monochrome Display
  OLED6 = OLED 128x64 I2C Monochrome Display
  OLED7 = OLED 128x64 I2C Monochrome Display
  Bauteil5 = Arduino Mega 2560 (Rev3)

nets:
  N1: Bauteil1.2SDA, OLED3.SDA
  N2: Bauteil1.2SCL, OLED3.SCK
  N3: Bauteil1.3SDA, OLED4.SDA
  N4: Bauteil1.3SCL, OLED4.SCK
  N5: Bauteil1.4SDA, OLED5.SDA
  N6: Bauteil1.4SCL, OLED5.SCK
  N7: Bauteil1.5SDA, OLED6.SDA
  N8: Bauteil1.5SCL, OLED6.SCK
  N9: Bauteil1.6SDA, OLED7.SDA
  N10: Bauteil1.6SCL, OLED7.SCK
  GND: Bauteil1.GND, OLED2.GND, OLED3.GND, OLED4.GND, OLED5.GND, OLED6.GND, OLED7.GND
  N11: Bauteil1.INPUTSDA, Bauteil5.D20/SDA
  N12: Bauteil1.INPUTSCL, Bauteil5.D21/SCL
  N13: Bauteil1.0SDA, OLED1.SDA
  N14: Bauteil1.0SCL, OLED1.SCK
  N15: Bauteil1.1SDA, OLED2.SDA
  N16: Bauteil1.1SCL, OLED2.SCK
  VDD: OLED1.VDD, OLED3.VDD, OLED4.VDD, OLED5.VDD, OLED6.VDD, OLED7.VDD

custom parts:
  Adafruit TCA9548A: You just found the perfect I2C sensor, and you want to wire up two or three or more of them to your Arduino when you realize "Uh oh, this chip has a fixed I2C address, and from what I know about I2C, you cannot have two devices with the same address on the same SDA/SCL pins!" Are you out of luck? You would be, if you didn't have this ultra-cool TCA9548A 1-to-8 I2C multiplexer! Finally, a way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
